// Logisim project arq_mips.circ as structural Verilog: 1 circuit, main circuit main
module main (
  input  [3:0] ALUOp,
  input  REGWrite,
  input  REGDst,
  input  Reset
);

  wire CLK, registerfile_1_p1, registerfile_1_p6, registerfile_1_p7;
  wire [4:0] multiplexer_1_out;
  wire [31:0] adder_1_out, mipsprogramrom_1_p2, PC_q;

  Clock clock_1 (.out(CLK));
  Register #(.width(32)) PC (.D(adder_1_out), .en(1'b1), .clk(CLK), .Q(PC_q), .clr(Reset));
  Adder #(.width(32)) adder_1 (.a(32'h4), .b(PC_q), .out(adder_1_out));  // open: cin, cout
  // MIPSProgramROM mipsprogramrom_1: pin names not known; wires that end beside it: PC_q, mipsprogramrom_1_p2, CLK
  Multiplexer #(.width(5), .enable("false")) multiplexer_1 (
    .in0(mipsprogramrom_1_p2[20:16]), .in1(mipsprogramrom_1_p2[15:11]), .out(multiplexer_1_out), .sel(REGDst));
  // RegisterFile registerfile_1: pin names not known; wires that end beside it: registerfile_1_p1, REGWrite, multiplexer_1_out, mipsprogramrom_1_p2[25:21], mipsprogramrom_1_p2[20:16], registerfile_1_p6, registerfile_1_p7
  // Mips_ALU mips_alu_1: pin names not known; wires that end beside it: registerfile_1_p6, registerfile_1_p7, ALUOp, registerfile_1_p1
endmodule
