// Logisim project mips_1.circ as structural Verilog: 1 circuit, main circuit main
module main (
  input  in_1,
  input  in_2,
  input  in_3,
  input  in_4,
  input  [3:0] in_5,
  input  in_6,
  input  in_7,
  input  in_8,
  input  Branch,
  output [31:0] out_10,
  output [31:0] out_11,
  output [31:0] out_12,
  output [4:0] out_13,
  output [31:0] out_14,
  output [4:0] out_15,
  output [4:0] out_16
);

  wire CLK;
  wire [11:0] mips_alu_1_p5_2;
  wire [19:0] mips_alu_1_p5;
  wire [31:0] adder_1_out, adder_2_out, bit_extender_1_out, mips_ram_1_p8, mipsprogramrom_1_p2,
       multiplexer_1_out, PC_q, shifter_1_out;

  Register #(.width(32)) PC (.D(multiplexer_1_out), .en(1'b1), .clk(CLK), .Q(PC_q), .clr(in_1));
  Clock clock_1 (.out(CLK));
  Adder #(.width(32)) adder_1 (.a(32'h4), .b(PC_q), .out(adder_1_out));  // open: cin, cout
  Multiplexer #(.width(32), .enable("false")) multiplexer_1 (
    .in0(adder_1_out), .in1(adder_2_out), .out(multiplexer_1_out), .sel(Branch));
  Adder #(.width(32)) adder_2 (.a(adder_1_out), .b(shifter_1_out), .out(adder_2_out));  // open: cin, cout
  // MIPSProgramROM mipsprogramrom_1: pin names not known; wires that end beside it: PC_q, {mipsprogramrom_1_p2[31:26], out_15, out_13, mipsprogramrom_1_p2[15:0]}, adder_2_out
  Shifter #(.width(32)) shifter_1 (.in(bit_extender_1_out), .\dist (5'b00010), .out(shifter_1_out));
  assign bit_extender_1_out = {{16{mipsprogramrom_1_p2[15]}}, mipsprogramrom_1_p2[15:0]};  // Bit_Extender bit_extender_1
  Multiplexer #(.width(5), .enable("false")) multiplexer_2 (
    .in0(out_13), .in1(mipsprogramrom_1_p2[15:11]), .out(out_16), .sel(in_3));
  // RegisterFile registerfile_1: pin names not known; wires that end beside it: out_10, CLK, in_2, out_16, out_15, out_13, out_11, out_14
  Multiplexer #(.width(32), .enable("false")) multiplexer_3 (
    .in0(out_14), .in1(bit_extender_1_out), .out(out_12), .sel(in_4));
  // Mips_ALU mips_alu_1: pin names not known; wires that end beside it: out_11, out_12, in_5, mipsprogramrom_1_p2[10:6], {mips_alu_1_p5_2, mips_alu_1_p5}
  // MIPS_RAM mips_ram_1: pin names not known; wires that end beside it: mips_alu_1_p5, out_14, in_6, 4'b1111, CLK, in_7, in_1, mips_ram_1_p8
  Multiplexer #(.width(32), .enable("false")) multiplexer_4 (
    .in0(mips_ram_1_p8), .in1({mips_alu_1_p5_2, mips_alu_1_p5}), .out(out_10), .sel(in_8));

  // Other names for the same wires on the sheet: ALUOp[3:0] = in_5; ALUSrc = in_4; MemRead = in_7; MemToReg = in_8;
  //   MemWrite = in_6; REGDest = in_3; REGWrite = in_2; RST = in_1

  // Notes on the sheet:
  //   contents of mipsprogramrom_1 (hex, n*v repeats v):
  //   subu $9, $16, $10 addu $9, $8, $8
endmodule
