// Logisim project lobo_guara.circ as structural Verilog: 18 circuits, main circuit main
module main (
  input  RST,
  output [7:0] out_2,
  output [7:0] out_3,
  output [3:0] out_4,
  output [3:0] out_5,
  output [7:0] out_6,
  output [7:0] out_7,
  output [7:0] out_8,
  output [7:0] out_9,
  output [7:0] out_10,
  output [7:0] out_11
);

  wire ALUSrc, and_1_out, Branch, BranchSrc, CLK, Jump, MemRead, MemtoReg, MemWrite, or_1_out, RegDST,
       RegWrite, Zero;
  wire [1:0] multiplexer_2_out;
  wire [7:0] adder_1_out, bit_extender_1_out, bit_extender_2_out, multiplexer_1_out;

  Clock u_CLK (.out(CLK));
  Multiplexer #(.width(8), .enable("false")) multiplexer_1 (
    .in0(out_11), .in1(out_9), .out(multiplexer_1_out), .sel(MemtoReg));
  assign bit_extender_1_out = {{4{1'b0}}, out_3[3:0]};  // Bit_Extender bit_extender_1
  and and_1 (and_1_out, Branch, Zero);
  MI mi_1 (.PC(out_6), .OP(out_3));
  Multiplexer #(.width(2), .enable("false")) multiplexer_2 (
    .in0(out_3[3:2]), .in1(2'b01), .out(multiplexer_2_out), .sel(RegDST));
  Multiplexer #(.width(8), .enable("false")) multiplexer_3 (
    .in0(out_7), .in1(bit_extender_1_out), .out(out_10), .sel(ALUSrc));
  assign bit_extender_2_out = {{4{out_3[3]}}, out_3[3:0]};  // Bit_Extender bit_extender_2
  Multiplexer #(.width(8), .enable("false")) multiplexer_4 (
    .in0(out_7), .in1(adder_1_out), .out(out_2), .sel(BranchSrc));
  or or_1 (or_1_out, and_1_out, Jump);
  Registradores registradores_1 (
    .rA(multiplexer_2_out), .rB(out_3[1:0]), .W(multiplexer_1_out), .WE(RegWrite), .RST(RST), .CLK(CLK),
    .A(out_8), .B(out_7));
  Adder adder_1 (.a(bit_extender_2_out), .b(out_6), .out(adder_1_out));  // open: cin, cout
  ULA ula_1 (.A(out_8), .B(out_10), .ALUOp(out_4), .C(out_11), .Zero(Zero));
  IR ir_1 (.PCin(out_2), .Branch(or_1_out), .CLK(CLK), .RST(RST), .PCout(out_6));
  UC uc_1 (
    .Op(out_3[7:4]), .Branch(Branch), .MemRead(MemRead), .BranchSrc(BranchSrc), .ALUOp(out_4),
    .MemWrite(MemWrite), .ALUSrc(ALUSrc), .RegWrite(RegWrite), .RegDST(RegDST), .MemtoReg(MemtoReg),
    .Jump(Jump));
  MP mp_1 (.MemRead(MemRead), .MemWrite(MemWrite), .Address(out_7), .DIN(out_8), .CLK(CLK), .DOUT(out_9));

  assign out_5 = out_3[7:4];

  // Other names for the same wires on the sheet: A[7:0] = out_8; ALUOp[3:0] = out_4; B[7:0] = out_7; C[7:0] = out_11;
  //   Dout[7:0] = out_9; Imm[3:0] = out_3[3:0]; rB[1:0] = out_3[1:0]; rA[1:0] = out_3[3:2]; OP[3:0] = out_3[7:4];
  //   PCout[7:0] = out_6
endmodule

module Registradores (
  input  [1:0] rA,
  input  [1:0] rB,
  input  [7:0] W,
  input  WE,
  input  RST,
  input  CLK,
  output [7:0] A,
  output [7:0] B
);

  wire demultiplexer_1_out0, demultiplexer_1_out1, demultiplexer_1_out2, demultiplexer_1_out3;
  wire [7:0] r0_q, r1_q, r2_q, r3_q;

  Demultiplexer #(.select(2), .enable("false")) demultiplexer_1 (
    .out0(demultiplexer_1_out0), .out1(demultiplexer_1_out1), .out2(demultiplexer_1_out2),
    .out3(demultiplexer_1_out3), .in(WE), .sel(rA));
  Register r0 (.D(W), .en(demultiplexer_1_out0), .clk(CLK), .Q(r0_q), .clr(CLK));
  Register r1 (.D(W), .en(demultiplexer_1_out1), .clk(CLK), .Q(r1_q), .clr(RST));
  Register r2 (.D(W), .en(demultiplexer_1_out2), .clk(CLK), .Q(r2_q), .clr(RST));
  Register r3 (.D(W), .en(demultiplexer_1_out3), .clk(CLK), .Q(r3_q), .clr(RST));
  Multiplexer #(.select(2), .width(8), .enable("false")) multiplexer_1 (
    .in0(r0_q), .in1(r1_q), .in2(r2_q), .in3(r3_q), .out(A), .sel(rA));
  Multiplexer #(.select(2), .width(8), .enable("false")) multiplexer_2 (
    .in0(r0_q), .in1(r1_q), .in2(r2_q), .in3(r3_q), .out(B), .sel(rB));

  // Notes on the sheet:
  //   Valor sempre zero
endmodule

module UC (
  input  [3:0] Op,
  output Branch,
  output MemRead,
  output BranchSrc,
  output [3:0] ALUOp,
  output MemWrite,
  output ALUSrc,
  output RegWrite,
  output RegDST,
  output MemtoReg,
  output Jump
);

  UC_Branch uc_branch_1 (.n4(Op[0]), .n5(Op[1]), .n6(Op[2]), .n7(Op[3]), .Branch(Branch));
  UC_MemRead uc_memread_1 (.n4(Op[0]), .n5(Op[1]), .n6(Op[2]), .n7(Op[3]), .MemRead(MemRead));
  UC_BranchSrc uc_branchsrc_1 (.n4(Op[0]), .n5(Op[1]), .n6(Op[2]), .n7(Op[3]), .BranchSrc(BranchSrc));
  UC_ALUOp uc_aluop_1 (.n4(Op[0]), .n5(Op[1]), .n6(Op[2]), .n7(Op[3]), .ALUOp(ALUOp));
  UC_MemWrite uc_memwrite_1 (.n4(Op[0]), .n5(Op[1]), .n6(Op[2]), .n7(Op[3]), .MemWrite(MemWrite));
  UC_ALUSrc uc_alusrc_1 (.n4(Op[0]), .n5(Op[1]), .n6(Op[2]), .n7(Op[3]), .ALUSrc(ALUSrc));
  UC_RegWrite uc_regwrite_1 (.n4(Op[0]), .n5(Op[1]), .n6(Op[2]), .n7(Op[3]), .RegWrite(RegWrite));
  UC_RegDST uc_regdst_1 (.n4(Op[0]), .n5(Op[1]), .n6(Op[2]), .n7(Op[3]), .RegDST(RegDST));
  UC_MemtoReg uc_memtoreg_1 (.n4(Op[0]), .n5(Op[1]), .n6(Op[2]), .n7(Op[3]), .MemtoReg(MemtoReg));
  UC_Jump uc_jump_1 (.n4(Op[0]), .n5(Op[1]), .n6(Op[2]), .n7(Op[3]), .Jump(Jump));
endmodule

module UC_simp (
  input  n7,
  input  n6,
  input  n5,
  input  n4,
  output Branch,
  output MemRead,
  output BranchSrc,
  output Jump,
  output MemWrite,
  output ALUSrc,
  output RegWrite,
  output RegDST,
  output MemtoReg
);

  wire and_3_out, and_5_out, and_6_out, and_8_out, and_9_out, and_10_out, and_11_out, and_12_out, not_1_out,
       not_2_out, not_3_out, not_4_out, not_5_out, not_6_out, not_7_out, not_8_out, not_9_out, not_10_out,
       not_11_out, not_12_out, not_13_out, not_14_out, not_15_out, not_16_out, not_17_out, not_18_out,
       not_19_out, not_20_out, not_21_out, not_22_out, not_23_out, not_24_out, not_25_out, not_26_out,
       not_27_out, not_28_out, not_29_out, not_30_out;

  not not_1 (not_1_out, n7);
  not not_2 (not_2_out, n6);
  and and_1 (Branch, not_1_out, not_2_out, not_3_out);
  not not_3 (not_3_out, n5);
  not not_4 (not_4_out, n7);
  not not_5 (not_5_out, n5);
  not not_6 (not_6_out, n4);
  not not_7 (not_7_out, n7);
  not not_8 (not_8_out, n6);
  not not_9 (not_9_out, n5);
  not not_10 (not_10_out, n4);
  not not_11 (not_11_out, n7);
  not not_12 (not_12_out, n6);
  not not_13 (not_13_out, n7);
  and and_2 (Jump, not_13_out, not_14_out, n5);
  not not_14 (not_14_out, n6);
  not not_15 (not_15_out, n7);
  not not_16 (not_16_out, n5);
  not not_17 (not_17_out, n7);
  not not_18 (not_18_out, n6);
  not not_19 (not_19_out, n5);
  not not_20 (not_20_out, n4);
  and and_3 (and_3_out, n6, n5);
  not not_21 (not_21_out, n7);
  not not_22 (not_22_out, n6);
  not not_23 (not_23_out, n5);
  not not_24 (not_24_out, n7);
  not not_25 (not_25_out, n6);
  not not_26 (not_26_out, n5);
  not not_27 (not_27_out, n4);
  not not_28 (not_28_out, n7);
  not not_29 (not_29_out, n5);
  not not_30 (not_30_out, n4);
  and and_4 (MemRead, not_4_out, n6, not_5_out, not_6_out);
  and and_5 (and_5_out, not_7_out, not_8_out, not_9_out, not_10_out);
  or or_1 (BranchSrc, and_5_out, and_6_out);
  and and_6 (and_6_out, not_11_out, not_12_out, n5, n4);
  and and_7 (MemWrite, not_15_out, n6, not_16_out, n4);
  and and_8 (and_8_out, not_17_out, n6, n5, n4);
  or or_2 (ALUSrc, and_8_out, and_9_out);
  and and_9 (and_9_out, n7, not_18_out, not_19_out, not_20_out);
  or or_3 (RegWrite, and_3_out, n7);
  and and_10 (and_10_out, not_21_out, not_22_out, not_23_out, n4);
  or or_4 (RegDST, and_10_out, and_11_out, and_12_out);
  and and_11 (and_11_out, not_24_out, n6, n5, n4);
  and and_12 (and_12_out, n7, not_25_out, not_26_out, not_27_out);
  and and_13 (MemtoReg, not_28_out, n6, not_29_out, not_30_out);
endmodule

module MI (
  input  [7:0] PC,
  output [7:0] OP
);

  ROM rom_1 (.addr(PC), .data(OP));

  // Notes on the sheet:
  //   contents of rom_1 (hex, n*v repeats v):
  //   83 69 88 f6
endmodule

module ULA (
  input  [7:0] A,
  input  [7:0] B,
  input  [3:0] ALUOp,
  output [7:0] C,
  output Zero
);

  wire [7:0] adder_1_out, adder_2_out, adder_3_out, and_1_out, bit_extender_1_out, bit_extender_2_out,
       not_1_out, or_1_out, shifter_1_out, shifter_2_out, shifter_3_out, shifter_4_out, subtractor_1_out;

  Adder adder_1 (.a(A), .b(B), .out(adder_1_out));  // open: cin, cout
  Subtractor subtractor_1 (.a(A), .b(B), .out(subtractor_1_out));  // open: bin, bout
  assign not_1_out = ~B;  // NOT_Gate not_1, 8 bits wide
  Shifter shifter_1 (.in(A), .\dist (B[2:0]), .out(shifter_1_out));
  Shifter #(.shift("lr")) shifter_2 (.in(A), .\dist (B[2:0]), .out(shifter_2_out));
  assign bit_extender_1_out = {{4{1'b0}}, A[3:0]};  // Bit_Extender bit_extender_1
  assign bit_extender_2_out = {{4{1'b0}}, A[7:4]};  // Bit_Extender bit_extender_2
  assign and_1_out = A & B;  // AND_Gate and_1, 8 bits wide
  assign or_1_out = A | B;  // OR_Gate or_1, 8 bits wide
  Shifter shifter_3 (.in(B), .\dist (3'b100), .out(shifter_3_out));
  Shifter shifter_4 (.in(bit_extender_2_out), .\dist (3'b100), .out(shifter_4_out));
  Adder adder_2 (.a(shifter_3_out), .b(bit_extender_1_out), .out(adder_2_out));  // open: cin, cout
  Multiplexer #(.select(4), .width(8), .enable("false")) multiplexer_1 (
    .in0(adder_1_out), .in1(subtractor_1_out), .in2(and_1_out), .in3(or_1_out), .in4(not_1_out),
    .in5(shifter_1_out), .in6(shifter_2_out), .in7(B), .in8(adder_2_out), .in9(adder_3_out), .in10(A),
    .out(C), .sel(ALUOp));  // open: in11, in12, in13, in14, in15
  Adder adder_3 (.a(B), .b(shifter_4_out), .out(adder_3_out));  // open: cin, cout
  Comparator comparator_1 (.a(C), .b({8{1'b0}}), .eq(Zero));  // open: gt, lt
endmodule

module UC_ALUOp (
  input  n4,
  input  n5,
  input  n6,
  input  n7,
  output [3:0] ALUOp
);

  wire and_1_out, and_2_out, and_3_out, and_4_out, and_5_out, and_6_out, and_7_out, and_8_out, and_9_out,
       and_10_out, and_11_out, and_12_out, not_1_out, not_2_out, not_3_out, not_4_out, not_5_out, not_6_out,
       not_7_out, not_8_out, not_9_out, not_10_out, not_11_out, not_12_out, not_13_out, not_14_out,
       not_15_out, not_16_out, not_17_out, not_18_out, not_19_out, not_20_out, not_21_out, not_22_out,
       or_1_out;

  not not_1 (not_1_out, n6);
  not not_2 (not_2_out, n5);
  not not_3 (not_3_out, n6);
  not not_4 (not_4_out, n4);
  not not_5 (not_5_out, n6);
  not not_6 (not_6_out, n5);
  not not_7 (not_7_out, n4);
  not not_8 (not_8_out, n5);
  not not_9 (not_9_out, n4);
  not not_10 (not_10_out, n7);
  not not_11 (not_11_out, n4);
  not not_12 (not_12_out, n7);
  not not_13 (not_13_out, n6);
  not not_14 (not_14_out, n5);
  not not_15 (not_15_out, n4);
  not not_16 (not_16_out, n7);
  not not_17 (not_17_out, n6);
  not not_18 (not_18_out, n5);
  not not_19 (not_19_out, n4);
  not not_20 (not_20_out, n7);
  not not_21 (not_21_out, n6);
  not not_22 (not_22_out, n5);
  and and_1 (and_1_out, n7, not_1_out, not_2_out, n4);
  and and_2 (and_2_out, n7, not_3_out, n5, not_4_out);
  and and_3 (and_3_out, n7, not_5_out, n5, n4);
  and and_4 (and_4_out, n7, n6, not_6_out, not_7_out);
  and and_5 (and_5_out, n7, n6, not_8_out, n4);
  and and_6 (and_6_out, n7, n6, n5, not_9_out);
  and and_7 (and_7_out, n7, n6, n5, n4);
  and and_8 (and_8_out, not_10_out, n6, n5, not_11_out);
  and and_9 (and_9_out, not_12_out, n6, n5, n4);
  and and_10 (and_10_out, n7, not_13_out, not_14_out, not_15_out);
  and and_11 (and_11_out, not_16_out, not_17_out, not_18_out, not_19_out);
  and and_12 (and_12_out, not_20_out, not_21_out, not_22_out, n4);
  Priority_Encoder #(.select(4)) priority_encoder_1 (
    .in0(and_1_out), .in1(and_2_out), .in2(and_3_out), .in3(and_4_out), .in4(and_5_out), .in5(and_6_out),
    .in6(and_7_out), .in7(and_8_out), .in8(and_9_out), .in9(and_10_out), .in10(or_1_out), .out(ALUOp));  // open: in11, in12, in13, in14, in15, gs, en_out, en_in
  or or_1 (or_1_out, and_11_out, and_12_out);

  // Notes on the sheet:
  //   1001
  //   1010
  //   1011
  //   1100
  //   1101
  //   1110
  //   1111
  //   0110
  //   0111
  //   1000
  //   0000
  //   0001
endmodule

module UC_Branch (
  input  n4,
  input  n5,
  input  n6,
  input  n7,
  output Branch
);

  wire and_1_out, and_2_out, not_1_out, not_2_out, not_3_out, not_4_out, not_5_out, not_6_out, not_7_out;

  not not_1 (not_1_out, n7);
  not not_2 (not_2_out, n6);
  not not_3 (not_3_out, n5);
  not not_4 (not_4_out, n4);
  not not_5 (not_5_out, n7);
  not not_6 (not_6_out, n6);
  not not_7 (not_7_out, n5);
  and and_1 (and_1_out, not_1_out, not_2_out, not_3_out, not_4_out);
  and and_2 (and_2_out, not_5_out, not_6_out, not_7_out, n4);
  or or_1 (Branch, and_1_out, and_2_out);

  // Notes on the sheet:
  //   0000
  //   0001
endmodule

module UC_MemRead (
  input  n4,
  input  n5,
  input  n6,
  input  n7,
  output MemRead
);

  wire not_1_out, not_2_out, not_3_out;

  not not_1 (not_1_out, n7);
  not not_2 (not_2_out, n5);
  not not_3 (not_3_out, n4);
  and and_1 (MemRead, not_1_out, n6, not_2_out, not_3_out);

  // Notes on the sheet:
  //   0100
endmodule

module UC_BranchSrc (
  input  n4,
  input  n5,
  input  n6,
  input  n7,
  output BranchSrc
);

  wire and_1_out, and_2_out, not_1_out, not_2_out, not_3_out, not_4_out, not_5_out;

  not not_1 (not_1_out, n7);
  not not_2 (not_2_out, n6);
  not not_3 (not_3_out, n5);
  not not_4 (not_4_out, n7);
  not not_5 (not_5_out, n6);
  and and_1 (and_1_out, not_1_out, not_2_out, not_3_out, n4);
  and and_2 (and_2_out, not_4_out, not_5_out, n5, n4);
  or or_1 (BranchSrc, and_1_out, and_2_out);

  // Notes on the sheet:
  //   0001
  //   0011
endmodule

module UC_Jump (
  input  n4,
  input  n5,
  input  n6,
  input  n7,
  output Jump
);

  wire and_1_out, and_2_out, not_1_out, not_2_out, not_3_out, not_4_out, not_5_out;

  not not_1 (not_1_out, n7);
  not not_2 (not_2_out, n6);
  not not_3 (not_3_out, n4);
  not not_4 (not_4_out, n7);
  not not_5 (not_5_out, n6);
  and and_1 (and_1_out, not_1_out, not_2_out, n5, not_3_out);
  and and_2 (and_2_out, not_4_out, not_5_out, n5, n4);
  or or_1 (Jump, and_1_out, and_2_out);

  // Notes on the sheet:
  //   0010
  //   0011
endmodule

module UC_MemWrite (
  input  n4,
  input  n5,
  input  n6,
  input  n7,
  output MemWrite
);

  wire not_1_out, not_2_out;

  not not_1 (not_1_out, n7);
  not not_2 (not_2_out, n5);
  and and_1 (MemWrite, not_1_out, n6, not_2_out, n4);

  // Notes on the sheet:
  //   0101
endmodule

module UC_ALUSrc (
  input  n4,
  input  n5,
  input  n6,
  input  n7,
  output ALUSrc
);

  wire and_1_out, and_2_out, not_1_out, not_2_out, not_3_out, not_4_out;

  not not_1 (not_1_out, n7);
  not not_2 (not_2_out, n6);
  not not_3 (not_3_out, n5);
  not not_4 (not_4_out, n4);
  and and_1 (and_1_out, not_1_out, n6, n5, n4);
  and and_2 (and_2_out, n7, not_2_out, not_3_out, not_4_out);
  or or_1 (ALUSrc, and_1_out, and_2_out);

  // Notes on the sheet:
  //   0111
  //   1000
endmodule

module UC_RegWrite (
  input  n4,
  input  n5,
  input  n6,
  input  n7,
  output RegWrite
);

  wire and_1_out, and_2_out, and_3_out, and_4_out, and_5_out, and_6_out, and_7_out, and_8_out, and_9_out,
       and_10_out, and_11_out, not_1_out, not_2_out, not_3_out, not_4_out, not_5_out, not_6_out, not_7_out,
       not_8_out, not_9_out, not_10_out, not_11_out, not_12_out, not_13_out, not_14_out, not_15_out,
       not_16_out, not_17_out, not_18_out;

  not not_1 (not_1_out, n7);
  and and_1 (and_1_out, not_1_out, n6, n5, not_2_out);
  not not_2 (not_2_out, n4);
  not not_3 (not_3_out, n7);
  and and_2 (and_2_out, not_3_out, n6, n5, n4);
  not not_4 (not_4_out, n6);
  and and_3 (and_3_out, n7, not_4_out, not_5_out, not_6_out);
  not not_5 (not_5_out, n5);
  not not_6 (not_6_out, n4);
  not not_7 (not_7_out, n6);
  and and_4 (and_4_out, n7, not_7_out, not_8_out, n4);
  not not_8 (not_8_out, n5);
  not not_9 (not_9_out, n6);
  and and_5 (and_5_out, n7, not_9_out, n5, not_10_out);
  not not_10 (not_10_out, n4);
  not not_11 (not_11_out, n6);
  and and_6 (and_6_out, n7, not_11_out, n5, n4);
  and and_7 (and_7_out, n7, n6, not_12_out, not_13_out);
  not not_12 (not_12_out, n5);
  not not_13 (not_13_out, n4);
  and and_8 (and_8_out, n7, n6, not_14_out, n4);
  not not_14 (not_14_out, n5);
  and and_9 (and_9_out, n7, n6, n5, not_15_out);
  not not_15 (not_15_out, n4);
  and and_10 (and_10_out, n7, n6, n5, n4);
  not not_16 (not_16_out, n7);
  and and_11 (and_11_out, not_16_out, n6, not_17_out, not_18_out);
  not not_17 (not_17_out, n5);
  not not_18 (not_18_out, n4);
  or or_1 (RegWrite, and_1_out, and_2_out, and_3_out, and_4_out, and_5_out, and_11_out, and_6_out, and_7_out, and_8_out, and_9_out, and_10_out);

  // Notes on the sheet:
  //   0110
  //   0111
  //   1000
  //   1001
  //   1010
  //   1011
  //   1100
  //   1101
  //   1110
  //   1111
  //   0100
endmodule

module UC_RegDST (
  input  n4,
  input  n5,
  input  n6,
  input  n7,
  output RegDST
);

  wire and_1_out, and_2_out, and_3_out, not_1_out, not_2_out, not_3_out, not_4_out, not_5_out, not_6_out,
       not_7_out;

  not not_1 (not_1_out, n7);
  not not_2 (not_2_out, n6);
  not not_3 (not_3_out, n5);
  not not_4 (not_4_out, n4);
  not not_5 (not_5_out, n7);
  not not_6 (not_6_out, n6);
  not not_7 (not_7_out, n5);
  and and_1 (and_1_out, not_1_out, n6, n5, n4);
  and and_2 (and_2_out, n7, not_2_out, not_3_out, not_4_out);
  and and_3 (and_3_out, not_5_out, not_6_out, not_7_out, n4);
  or or_1 (RegDST, and_1_out, and_2_out, and_3_out);

  // Notes on the sheet:
  //   0111
  //   1000
  //   0001
endmodule

module UC_MemtoReg (
  input  n4,
  input  n5,
  input  n6,
  input  n7,
  output MemtoReg
);

  wire not_1_out, not_2_out, not_3_out;

  not not_1 (not_1_out, n7);
  not not_2 (not_2_out, n5);
  not not_3 (not_3_out, n4);
  and and_1 (MemtoReg, not_1_out, n6, not_2_out, not_3_out);

  // Notes on the sheet:
  //   0100
endmodule

module MP (
  input  MemRead,
  input  MemWrite,
  input  [7:0] Address,
  input  [7:0] DIN,
  input  CLK,
  output [7:0] DOUT
);

  wire [7:0] ram_1_data;

  RAM ram_1 (.addr(Address), .we(MemWrite), .oe(MemRead), .clk(CLK), .data(ram_1_data));
  Demultiplexer #(.width(8), .enable("false")) demultiplexer_1 (
    .out1(DOUT), .in(ram_1_data), .sel(MemRead));  // open: out0
  Multiplexer #(.width(8), .enable("false")) multiplexer_1 (.in1(DIN), .out(ram_1_data), .sel(MemWrite));  // open: in0
endmodule

module IR (
  input  [7:0] PCin,
  input  Branch,
  input  CLK,
  input  RST,
  output [7:0] PCout
);

  wire [7:0] adder_1_out, multiplexer_1_out;

  Register PC (.D(multiplexer_1_out), .en(1'b1), .clk(CLK), .Q(PCout), .clr(RST));
  Multiplexer #(.width(8), .enable("false")) multiplexer_1 (
    .in0(adder_1_out), .in1(PCin), .out(multiplexer_1_out), .sel(Branch));
  Adder adder_1 (.a(8'h1), .b(PCout), .out(adder_1_out));  // open: cin, cout
endmodule
